// Logisim project Projeto.circ as structural Verilog: 9 circuits, main circuit Apresentação
module \Apresentação  (
  input  Clear,
  output Overflow,
  output Zero
);

  wire Clock_out, microprocessador_1_store_pulso, not_1_out;
  wire [4:0] microprocessador_1_op_code, microprocessador_1_sel_rx, microprocessador_1_sel_ry,
       microprocessador_1_sel_write;
  wire [9:0] \microprocessador_1_endereço , \microprocessador_1_load_store_endereço ;
  wire [11:0] microprocessador_1_imm;
  wire [31:0] microprocessador_1_r, microprocessador_1_rx, microprocessador_1_ry,
       microprocessador_1_store_data, ram_1_data, ram_2_data;

  RAM #(.addrWidth(10), .dataWidth(32)) ram_1 (
    .addr(\microprocessador_1_endereço ), .data(ram_1_data));  // open: sel, clk, ld, clr
  RAM #(.addrWidth(10), .dataWidth(32)) ram_2 (
    .addr(\microprocessador_1_load_store_endereço ), .data(ram_2_data), .clk(Clock_out), .ld(not_1_out));  // open: sel, clr
  not not_1 (not_1_out, microprocessador_1_store_pulso);
  assign ram_2_data = microprocessador_1_store_pulso ? microprocessador_1_store_data : 32'bz;  // Controlled_Buffer controlled_buffer_1
  Clock Clock (.out(Clock_out));
  // Probe on microprocessador_1_rx
  // Probe on microprocessador_1_sel_write
  // Probe on microprocessador_1_ry
  MicroProcessador microprocessador_1 (
    .\Endereço (\microprocessador_1_endereço ), .Palavra(ram_1_data), .Write(Clock_out), .Clear(Clear),
    .Sel_Write(microprocessador_1_sel_write), .Sel_Rx(microprocessador_1_sel_rx), .R(microprocessador_1_r),
    .Overflow(Overflow), .Zero(Zero), .Sel_Ry(microprocessador_1_sel_ry), .Rx(microprocessador_1_rx),
    .Ry(microprocessador_1_ry), .IMM(microprocessador_1_imm), .Op_Code(microprocessador_1_op_code),
    .\Load_Store_Endereço (\microprocessador_1_load_store_endereço ), .Load_Data(ram_2_data),
    .Store_Data(microprocessador_1_store_data), .Store_Pulso(microprocessador_1_store_pulso));
  // Probe on microprocessador_1_imm
  // Probe on microprocessador_1_op_code
  // Probe on microprocessador_1_sel_rx
  // Probe on microprocessador_1_sel_ry
  // Probe on microprocessador_1_r
endmodule

module MicroProcessador (
  input  [31:0] Palavra,
  input  [31:0] Load_Data,
  input  Write,
  input  Clear,
  output [31:0] Rx,
  output [31:0] Ry,
  output [4:0] Sel_Rx,
  output [31:0] R,
  output [4:0] Sel_Write,
  output Overflow,
  output Zero,
  output [31:0] Store_Data,
  output [4:0] Sel_Ry,
  output [11:0] IMM,
  output [4:0] Op_Code,
  output [9:0] \Load_Store_Endereço ,
  output [9:0] \Endereço ,
  output Store_Pulso
);

  wire io_dp_1_io___dp, not_1_out, store_ou_load_1_store___load;
  wire [31:0] banco_de_registradores_1_ry, \entrada_br_1_saída , extensor_de_sinal_1_out_2, multiplexer_1_out;

  Leitor_da_Palavra leitor_da_palavra_1 (
    .Entrada(Palavra), .IMM(IMM), .Sel_Ry(Sel_Ry), .Sel_Rx(Sel_Rx), .Sel_Write(Sel_Write), .Op_Code(Op_Code));
  Entrada_BR entrada_br_1 (.OpCode(Op_Code), .ULA_S(R), .Load_Dado(Load_Data), .\Saída (\entrada_br_1_saída ));
  not not_1 (not_1_out, Write);
  Banco_de_Registradores banco_de_registradores_1 (
    .DataIn(\entrada_br_1_saída ), .Write(Write), .Rx(Rx), .Ry(banco_de_registradores_1_ry),
    .Sel_Write(Sel_Write), .Sel_Rx(Sel_Rx), .Sel_Ry(Sel_Ry));
  Extensor_de_Sinal extensor_de_sinal_1 (.in_1(IMM), .out_2(extensor_de_sinal_1_out_2));
  PC pc_1 (
    .Clock(not_1_out), .Clear(Clear), .Passo(10'h1), .\Endereço (\Endereço ), .Op_Code(Op_Code), .IMM(IMM),
    .Zero(Zero));
  Store_ou_Load store_ou_load_1 (.Op_Code(Op_Code), .Store___Load(store_ou_load_1_store___load));
  Multiplexer #(.width(32), .enable("false")) multiplexer_1 (
    .in0(Rx), .in1(banco_de_registradores_1_ry), .out(multiplexer_1_out), .sel(store_ou_load_1_store___load));
  Multiplexer #(.width(32), .enable("false")) multiplexer_2 (
    .in0(banco_de_registradores_1_ry), .in1(extensor_de_sinal_1_out_2), .out(Ry), .sel(io_dp_1_io___dp));
  IO_DP io_dp_1 (.Op_Sel(Op_Code), .IO___DP(io_dp_1_io___dp));
  Conjunto conjunto_1 (.A(multiplexer_1_out), .B(Ry), .S(R), .Sel(Op_Code), .Zero(Zero), .Overflow(Overflow));
  Store_Pulso store_pulso_1 (.Op_Code(Op_Code), .Pulso(Store_Pulso));
  Extensor_de_Sinal_32_10 extensor_de_sinal_32_10_1 (.out_2(\Load_Store_Endereço ), .in_1(R));

  assign Store_Data = Rx;

  // Notes on the sheet:
  //   Operações Base
  //   00000 AND 
  //   00001 OR
  //   00010 NAND
  //   00011 XOR
  //   00100 Somador Inteiros
  //   00101 Somador Naturais
  //   00110 Subtrator
  //   00111 Deslocamento Esquerda
  //   01000 Deslocamento Direita
  //   01001 Deslocamento Direita com Sinal
  //   01010 Rotação Esquerda
  //   01011 Rotação Direita
  //   01100 Menor que
  //   01101 JUMP
  //   01110 BEQ
  //   01111 BNQ
  //   Operações Novas
  //   11110  Load
  //   11111  Store
  //   Operações I
  //   10000 AND
  //   10001 OR
  //   10010 NAND
  //   10011 XOR
  //   10100 Somador Inteiros
  //   10101 Somador Naturais
  //   10110 Subtrator
  //   10111 Deslocamento Esquerda
  //   11000 Deslocamento Direita
  //   11001 Deslocamento Direita com Sinal
  //   11010 Rotação Esquerda
  //   11011 Rotação Direita
  //   11100  Menor que
endmodule

module IO_DP (
  input  [4:0] Op_Sel,
  output IO___DP
);


  assign IO___DP = Op_Sel[4];
  assign Op_Sel[2:0] = {3{Op_Sel[3]}};
  // also tied to GND on the sheet: Op_Sel[3]
endmodule

module Extensor_de_Sinal (
  input  [11:0] in_1,
  output [31:0] out_2
);


  assign out_2 = {{21{in_1[11]}}, in_1[10:0]};
endmodule

module Leitor_da_Palavra (
  input  [31:0] Entrada,
  output [11:0] IMM,
  output [4:0] Sel_Ry,
  output [4:0] Sel_Rx,
  output [4:0] Sel_Write,
  output [4:0] Op_Code
);


  assign IMM = Entrada[11:0];
  assign Op_Code = Entrada[31:27];
  assign Sel_Rx = Entrada[21:17];
  assign Sel_Ry = Entrada[16:12];
  assign Sel_Write = Entrada[26:22];
endmodule

module Extensor_de_Sinal_32_10 (
  input  [31:0] in_1,
  output [9:0] out_2
);


  assign in_1[30:10] = {21{in_1[31]}};
  assign out_2 = in_1[9:0];
endmodule

module Entrada_BR (
  input  [4:0] OpCode,
  input  [31:0] ULA_S,
  input  [31:0] Load_Dado,
  output [31:0] \Saída 
);

  wire and_1_out;

  and and_1 (and_1_out, ~OpCode[0], OpCode[1], OpCode[2], OpCode[3], OpCode[4]);  // AND_Gate
  Multiplexer #(.width(32), .enable("false")) multiplexer_1 (
    .in0(ULA_S), .in1(Load_Dado), .out(\Saída ), .sel(and_1_out));
endmodule

module Store_Pulso (
  input  [4:0] Op_Code,
  output Pulso
);

  and and_1 (Pulso, Op_Code[0], Op_Code[1], Op_Code[2], Op_Code[3], Op_Code[4]);
endmodule

module Store_ou_Load (
  input  [4:0] Op_Code,
  output Store___Load
);

  and and_1 (Store___Load, Op_Code[1], Op_Code[2], Op_Code[3], Op_Code[4]);
  // also tied to GND on the sheet: Op_Code[0]
endmodule
